# Fritzing sketch ScopeAnalogFrontend (saved by Fritzing 0.9.2b)
circuit board: 8.46667cm x 5.64444cm
breadboards: 1

parts:
  C2 = Electrolytic Capacitor [capacitance=0.47mF part_number=2 package="100 mil [THT, electrolytic]"]
  IC1 = IC, DIP package, 14 pins [chip_label=MCP6024]
  C3 = Ceramic Capacitor [capacitance=22µF package="100 mil [THT, multilayer]"]
  C4 = Electrolytic Capacitor [capacitance=0.47mF package="100 mil [THT, electrolytic]"]
  R1 = Resistor [tolerance=±5% resistance=150k part_number=1 package=THT]
  R2 = Resistor [tolerance=±5% resistance=10k package=THT]
  R3 = Resistor [tolerance=±5% resistance=50k part_number=f package=THT]
  R4 = Resistor [tolerance=±1% resistance=150k part_number=g package=THT]
  C5 = Ceramic Capacitor [capacitance=10nF package="100 mil [THT, multilayer]"]
  C6 = Ceramic Capacitor [capacitance=22µF package="100 mil [THT, multilayer]"]
  C7 = Ceramic Capacitor [capacitance=100nF package="100 mil [THT, multilayer]"]
  IC3 = IC, DIP package, 14 pins [chip_label=6S26]
  Part1 = Arduino Uno (Rev3)
  R5 = Resistor [tolerance=±5% resistance=10k package=THT]
  R6 = Resistor [tolerance=±5% resistance=10k package=THT]
  IC4 = IC, DIP package, 14 pins [chip_label=4922]
  R7 = Resistor [tolerance=±5% resistance=10k package=THT]

nets:
  N1: C2.-, IC1.pin11, C3.1, C4.-, R4.Pin_0, C5.0, C6.0, C7.0, IC3.pin9, Part1.GND, IC4.pin8, IC4.pin12
  N2: C2.+, IC1.pin4, C5.1, C6.1, C7.1, IC3.pin14, Part1.VIN, R5.Pin_0, R6.Pin_0, IC4.pin1, IC4.pin9, IC4.pin13, R7.Pin_0
  N3: IC1.pin5, R1.Pin_1, R2.Pin_0
  N4: IC1.pin6, R3.Pin_0, R4.Pin_1
  N5: IC1.pin7, R3.Pin_1, IC3.pin2
  N6: C3.0, C4.+, R2.Pin_1, IC3.pin8, IC4.pin14
  N7: IC3.pin10, R5.Pin_1
  N8: IC3.pin11, R6.Pin_1, IC4.pin5
  N9: IC3.pin13, IC4.pin4
  N10: IC4.pin3, R7.Pin_1

notes:
  Vcc/Vdd
  Voffset
  Vin
  Vout
