# Fritzing sketch schematic (saved by Fritzing 0.9.1b)
circuit board: 9.56709cm x 9.76499cm
breadboards: 1

parts:
  C7 = Ceramic Capacitor [capacitance=100nF package="100 mil [THT, multilayer]"]
  C3 = Ceramic Capacitor [capacitance=6pF package="100 mil [THT, multilayer]"]
  J1 = shrouded pin header, 20 pins [form="♂ (shrouded male)" part_number=Left]
  R6 = Resistor [tolerance=±5% resistance=68k package=THT]
  R5 = Resistor [tolerance=±5% resistance=6.8k package=THT]
  J2 = shrouded pin header, 20 pins [form="♂ (shrouded male)" part_number=Right]
  C2 = Variable Capacitor [capacitance=100nF max_capacitance=10pF min_capacitance=2pF voltage=35V]
  C2_2 = Electrolytic Capacitor [capacitance=0.22mF package="100 mil [THT, electrolytic]"]
  DAC2 = IC, DIP package, 14 pins [chip_label=4922]
  555 = General purpose bipolar Timer [package=dil-08]
  OPAMP = IC, DIP package, 14 pins [chip_label=6024]
  C8 = Ceramic Capacitor [capacitance=100nF package="100 mil [THT, multilayer]"]
  C3_2 = Electrolytic Capacitor [capacitance=0.22mF package="100 mil [THT, electrolytic]"]
  Cf1 = Variable Capacitor [capacitance=100nF max_capacitance=10pF min_capacitance=2pF voltage=35V]
  Cf2 = Variable Capacitor [capacitance=100nF max_capacitance=10pF min_capacitance=2pF voltage=35V]
  Rg1 = Resistor [tolerance=±1% resistance=1M package=THT]
  C5 = Ceramic Capacitor [capacitance=100nF package="100 mil [THT, multilayer]"]
  DAC1 = IC, DIP package, 14 pins [chip_label=4922]
  C6 = Ceramic Capacitor [capacitance=100nF package="100 mil [THT, multilayer]"]
  R4 = Resistor [tolerance=±1% resistance=69.8k package=THT]
  C4 = Variable Capacitor [capacitance=100nF max_capacitance=10pF min_capacitance=2pF voltage=35V]
  bnc2 = BNC [package=bnc]
  Rg2 = Resistor [tolerance=±1% resistance=1M package=THT]
  C1 = Ceramic Capacitor [capacitance=6pF package="100 mil [THT, multilayer]"]
  PGA2 = IC, DIP package, 14 pins [chip_label=6S26]
  C5_2 = Ceramic Capacitor [capacitance=10nF package="100 mil [THT, multilayer]"]
  C4_2 = Ceramic Capacitor [capacitance=100nF package="100 mil [THT, multilayer]"]
  R2 = Resistor [tolerance=±1% resistance=69.8k package=THT]
  Rf1 = Resistor [tolerance=±1% resistance=100k package=THT]
  PGA1 = IC, DIP package, 14 pins [chip_label=6S26]
  Rf2 = Resistor [tolerance=±1% resistance=100k package=THT]
  R1 = Resistor [tolerance=±1% resistance=931k package=THT]
  bnc1 = BNC [package=bnc]
  R3 = Resistor [tolerance=±1% resistance=931k package=THT]
  MUX = IC, DIP package, 16 pins [chip_label=IC part_number=74HC4051]

nets:
  GND: C7.0, J1.pin19, C2.0, C2_2.-, DAC2.pin8, DAC2.pin12, 555.GND, OPAMP.pin6, OPAMP.pin9, OPAMP.pin11, C8.0, C3_2.-, Rg1.Pin_0, C5.0, DAC1.pin8, DAC1.pin12, C6.0, C4.0, bnc2.GND, Rg2.Pin_0, PGA2.pin9, C5_2.0, C4_2.0, PGA1.pin9, bnc1.GND, MUX.pin6, MUX.pin7, MUX.pin8
  3.3V: C7.1, J1.pin1, DAC2.pin1, DAC2.pin9, DAC2.pin11, DAC2.pin13, OPAMP.pin4, OPAMP.pin5, OPAMP.pin10, C8.1, C3_2.+, C5.1, DAC1.pin1, DAC1.pin9, DAC1.pin11, DAC1.pin13, C6.1, PGA2.pin14, C4_2.1, PGA1.pin14, MUX.pin16
  IN+D: C3.0, OPAMP.pin12, R4.Pin_0, C4.1, R3.Pin_1
  N1: C3.1, bnc2.OUT, R3.Pin_0
  DACAOUTB: J1.pin5, DAC1.pin10
  CLK: J1.pin7, DAC2.pin4, DAC1.pin4, PGA2.pin13, PGA1.pin13
  PC7: J1.pin8, MUX.pin3
  CHB: J1.pin14, PGA2.pin1, MUX.pin14
  CHA: J1.pin18, MUX.pin13
  5V: J1.pin20, R5.Pin_1, C2_2.+, 555._RES, 555.VCC+
  N2: R6.Pin_0, 555.TRI, 555.TRE, C5_2.1
  N3: R6.Pin_1, R5.Pin_0, 555.DIS
  F1: J2.pin1, MUX.pin11
  F2: J2.pin2, MUX.pin10
  F3: J2.pin3, MUX.pin9
  DACBSS: J2.pin10, DAC2.pin3
  PGA1SS: J2.pin11, PGA1.pin12
  DACASS: J2.pin12, DAC1.pin3
  PGA2SS: J2.pin13, PGA2.pin12
  DATA: J2.pin15, DAC2.pin5, DAC1.pin5, PGA2.pin11, PGA1.pin11
  IN+A: C2.1, OPAMP.pin3
  DACBOUTB: DAC2.pin10, R4.Pin_1
  DACBOUTA: DAC2.pin14, R2.Pin_1
  OUTA/PGA1_IN1: OPAMP.pin1, Cf1.0, Rf1.Pin_1, PGA1.pin2
  IN-A: OPAMP.pin2, Cf1.1, Rg1.Pin_1, Rf1.Pin_0
  IN-D: OPAMP.pin13, Cf2.1, Rg2.Pin_1, Rf2.Pin_0
  OUTD/PGA2_IN1: OPAMP.pin14, Cf2.0, PGA2.pin2, Rf2.Pin_1
  DACAOUTA: DAC1.pin14, PGA2.pin8, PGA1.pin8
  N4: C1.0, R2.Pin_0, R1.Pin_1
  N5: C1.1, R1.Pin_0, bnc1.OUT
